# Fritzing sketch serialPortWiring (saved by Fritzing 0.9.3b)
breadboards: 1

parts:
  Part1 = Arduino Uno (Rev3)
  Part2 = Arduino Uno (Rev3)
  Part3 = Arduino Uno (Rev3)

nets:
  N1: Part1.D0/RX, Part2.D0/RX, Part3.D1/TX
  N2: Part1.D1/TX, Part2.D1/TX, Part3.D0/RX
